# Fritzing sketch DulceriaArduino (saved by Fritzing 0.9.3b)
circuit board: 8.46667cm x 5.64444cm
breadboards: 1

parts:
  Componente1 = Arduino Mega 2560 (Rev3)
  S3 = Pushbutton [package=THT]
  S4 = Pushbutton [package=THT]
  S5 = Pushbutton [package=THT]
  S6 = Pushbutton [package=THT]
  R6 = Resistor [tolerance=±5% resistance=220 package=THT]
  R7 = Resistor [tolerance=±5% resistance=220 package=THT]
  R8 = Resistor [tolerance=±5% resistance=220 package=THT]
  R9 = Resistor [tolerance=±5% resistance=220 package=THT]
  LED1 = LED - 5mm [color="Red (633nm)" package="5 mm [THT]"]
  LED2 = LED - 5mm [color="Red (633nm)" package="5 mm [THT]"]
  LED3 = LED - 5mm [color="Red (633nm)" package="5 mm [THT]"]
  LED4 = LED - 5mm [color="Red (633nm)" package="5 mm [THT]"]
  R10 = Resistor [tolerance=±5% resistance=220 package=THT]
  R11 = Resistor [tolerance=±5% resistance=220 package=THT]
  R12 = Resistor [tolerance=±5% resistance=220 package=THT]
  R13 = Resistor [tolerance=±5% resistance=220 package=THT]
  U1 = CNZ1120 [package=cnz1120]
  R14 = Resistor [tolerance=±5% resistance=220 package=THT]
  R15 = Resistor [tolerance=±5% resistance=220 package=THT]

nets:
  N1: Componente1.D21/SCL, S3.leg0, R9.Pin_1
  N2: Componente1.D20/SDA, S4.leg0, R8.Pin_1
  N3: Componente1.D19/RX1, S5.leg0, R7.Pin_1
  N4: Componente1.D18/TX1, S6.leg0, R6.Pin_1
  N5: Componente1.5V, U1.2, R14.Pin_1
  N6: Componente1.GND, R6.Pin_0, R7.Pin_0, R8.Pin_0, R9.Pin_0, LED1.cathode, LED2.cathode, LED3.cathode, LED4.cathode, U1.4, R15.Pin_0
  N7: Componente1.D2_PWM, U1.3, R14.Pin_0
  N8: Componente1.D4_PWM, LED2.anode, R10.Pin_0, R10.Pin_1
  N9: Componente1.D5_PWM, LED1.anode, R11.Pin_0, R11.Pin_1
  N10: Componente1.D6_PWM, LED3.anode, R13.Pin_0, R13.Pin_1
  N11: Componente1.D7_PWM, LED4.anode, R12.Pin_0, R12.Pin_1
  N12: U1.1, R15.Pin_1
